# Fritzing sketch pi3-camera-trigger-breadboard (saved by Fritzing 0.9.3b)
breadboards: 1

parts:
  Raspberry_Pi_1 = Raspberry Pi B+
  Q1 = NPN-Transistor [package="TO92 [THT]"]
  R1 = Resistor [tolerance=±5% resistance=470 package=THT]
  To_Canon_Shutter_Connector = 2.5mm Audio Jack [package=stereojack2.5mm_specia_pogopins]
  Q2 = NPN-Transistor [package="TO92 [THT]"]
  R2 = Resistor [tolerance=±5% resistance=470 package=THT]
  PIR_Motion_Detector = PIR sensor

nets:
  N1: Raspberry_Pi_1.GPIO27, Q2.B
  GND: Raspberry_Pi_1.GND, Q1.E, To_Canon_Shutter_Connector.SLEEVE, Q2.E, PIR_Motion_Detector.GND
  N2: Raspberry_Pi_1.GPIO23, PIR_Motion_Detector.SIG
  N3: Raspberry_Pi_1.GPIO18, Q1.B
  5V: Raspberry_Pi_1.5V, PIR_Motion_Detector.VDD
  N4: Q1.C, R1.Pin_0
  N5: R1.Pin_1, To_Canon_Shutter_Connector.LEFT
  N6: To_Canon_Shutter_Connector.RIGHT, R2.Pin_1
  N7: Q2.C, R2.Pin_0
