# Fritzing sketch pi3-camera-trigger-hat (saved by Fritzing 0.9.3b)
circuit board: 6.53588cm x 5.69481cm

parts:
  PIR_Motion_Detector = PIR sensor
  Q3 = NPN-Transistor [package="TO92 [THT]"]
  R3 = Resistor [tolerance=±5% resistance=470 package=THT]
  Q4 = NPN-Transistor [package="TO92 [THT]"]
  R4 = Resistor [tolerance=±5% resistance=470 package=THT]
  To_Canon_Shutter_Connector1 = 2.5mm Audio Jack [package=stereojack2.5mm_specia_pogopins]
  Raspberry_Pi_1 = Raspberry Pi B+
  Part1 = Adafruit Perma-Proto HAT [part_number="Adafruit #2314 and #2310"]

nets:
  VDD: PIR_Motion_Detector.VDD, Raspberry_Pi_1.5V, Part1.5.0V
  N1: PIR_Motion_Detector.SIG, Part1.N$9#196
  GND: PIR_Motion_Detector.GND, Q3.E, Q4.E, To_Canon_Shutter_Connector1.SLEEVE, Raspberry_Pi_1.GND, Part1.GND
  N2: Q3.B, Part1.N$61#372
  N3: Q3.C, Part1.N$59#362
  N4: R3.Pin_0, Part1.N$59#364
  N5: R3.Pin_1, Part1.N$3#170
  N6: Q4.B, Part1.N$58#357
  N7: Q4.C, Part1.N$57#352
  N8: R4.Pin_0, Part1.N$57#354
  N9: R4.Pin_1, Part1.N$6#185
  N10: To_Canon_Shutter_Connector1.LEFT, Part1.N$3#166
  N11: To_Canon_Shutter_Connector1.RIGHT, Part1.N$6#181
  N12: Raspberry_Pi_1.GPIO27, Part1.GPIO27, Part1.N$58#356
  N13: Raspberry_Pi_1.GPIO23, Part1.GPIO23, Part1.N$9#200
  N14: Raspberry_Pi_1.GPIO18, Part1.GPIO18, Part1.N$61#371

custom parts:
  Adafruit Perma-Proto HAT: To kick off the Adafruit HAT party, we have this Perma-Proto inspired plug in daughter board. It has a grid of 0.1" prototyping soldering holes for attaching chips, resistors, LED, potentiometers and more. The holes are connected underneath with traces to mimic the solderless breadboards you're familiar. There's also long power strips for +3V, +5V and Ground connections to the Pi. Near the top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
